# Fritzing sketch RubberJogi (saved by Fritzing 0.9.4)

parts:
  Part3 = Arduino Micro (Rev3)
  Part4 = FTDI Basic Programmer

nets:
  N1: Part3.D1/TX, Part4.RXI
  N2: Part3.D0/RX, Part4.TXO
  GND: Part3.GND, Part4.GND
