# Fritzing sketch RubberJogi_with_4_switches (saved by Fritzing 0.9.4)

parts:
  Part3 = Arduino Micro (Rev3)
  Part4 = FTDI Basic Programmer
  U1 = Optocoupler [package=THT]
  U2 = Optocoupler [package=THT]
  R2 = Resistor [tolerance=±5% resistance=390 package=THT]
  R3 = Resistor [tolerance=±5% resistance=390 package=THT]
  JP1 = Header 2 [package=jst-2-pth-kit]
  JP2 = Header 2 [package=jst-2-pth-kit]
  U3 = Optocoupler [package=THT]
  JP3 = Header 2 [package=jst-2-pth-kit]
  R4 = Resistor [tolerance=±5% resistance=390 package=THT]
  U4 = Optocoupler [package=THT]
  JP4 = Header 2 [package=jst-2-pth-kit]
  R5 = Resistor [tolerance=±5% resistance=390 package=THT]

nets:
  N1: Part3.D1/TX, Part4.RXI
  N2: Part3.D0/RX, Part4.TXO
  GND: Part3.GND, Part4.GND, U1.Pin_2, U2.Pin_2, U3.Pin_2, U4.Pin_2
  N3: Part3.D2/SDA, R3.Pin_0
  N4: Part3.D4_PWM/A6, R2.Pin_0
  N5: Part3.D6_PWM/A7, R4.Pin_0
  N6: Part3.D8_PWM/A8, R5.Pin_0
  N7: Part3.5V, Part4.POWER
  N8: U1.Pin_1, R3.Pin_1
  N9: U1.Pin_4, JP1.2
  N10: U1.Pin_5, JP1.1
  N11: U2.Pin_1, R2.Pin_1
  N12: U2.Pin_4, JP2.2
  N13: U2.Pin_5, JP2.1
  N14: U3.Pin_1, R4.Pin_1
  N15: U3.Pin_4, JP3.2
  N16: U3.Pin_5, JP3.1
  N17: U4.Pin_1, R5.Pin_1
  N18: U4.Pin_4, JP4.2
  N19: U4.Pin_5, JP4.1
