# Fritzing sketch RubberJogi_with_switch (saved by Fritzing 0.9.4)

parts:
  Part3 = Arduino Micro (Rev3)
  Part4 = FTDI Basic Programmer
  U1 = Optocoupler [package=THT]
  U2 = Optocoupler [package=THT]
  R2 = Resistor [tolerance=±5% resistance=390 package=THT]
  R3 = Resistor [tolerance=±5% resistance=390 package=THT]
  JP1 = Header 2 [package=jst-2-pth-kit]
  JP2 = Header 2 [package=jst-2-pth-kit]

nets:
  N1: Part3.D1/TX, Part4.RXI
  N2: Part3.D0/RX, Part4.TXO
  GND: Part3.GND, Part4.GND, U1.Pin_2, U2.Pin_2
  N3: Part3.D2/SDA, R3.Pin_0
  N4: Part3.D4_PWM/A6, R2.Pin_0
  N5: Part3.5V, Part4.POWER
  N6: U1.Pin_1, R3.Pin_1
  N7: U1.Pin_4, JP1.2
  N8: U1.Pin_5, JP1.1
  N9: U2.Pin_1, R2.Pin_1
  N10: U2.Pin_4, JP2.2
  N11: U2.Pin_5, JP2.1
